# Fritzing sketch circuit diagram (saved by Fritzing 0.9.2b)
breadboards: 1

parts:
  U1 = ESP32S-HiLetgo [part_number=ESP32S-HiLetgo]
  J1 = Piezo Speaker
  Water_Level_Sensor1 = Water Level Sensor
  Part1 = LCD1602-I2C

nets:
  N1: U1.GPIO36, Water_Level_Sensor1.SIG
  GND: U1.GND, J1.pin1, Water_Level_Sensor1.GND, Part1.GND
  VIN: U1.VIN, Part1.VCC
  N2: U1.GPIO2, J1.pin2
  N3: U1.GPIO17, Water_Level_Sensor1.VCC
  N4: U1.GPIO21, Part1.SDA
  N5: U1.GPIO22, Part1.SCL

custom parts:
  ESP32S-HiLetgo: HiLetgo ESP-WROOM-32 ESP32 ESP-32S Development Board 2.4GHz Dual-Mode WiFi + Bluetooth Dual Cores Microcontroller The ESP32 integrated with Antenna switches, RF Balun, power amplifiers, low-noise amplifiers, filters, and management modules, and the entire solution occupies the least area of PCB. 2.4 GHz Wi-Fi plus Bluetooth dual-mode chip, with TSMC Ultra-low power consumption 40nm technology,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
  Water Level Sensor: A water level sensor. This sensor operates at 3V to 5V. The Sig (signal) pin outputs an analogue signal that is in proportion to the amount of water in contact with the sensor.
  LCD1602-I2C: A standard character display, usually with 2x16 characters. Comes in many colors with LCM1602 IIC attached.
